// Logisim project Ilyes_Kouachi_cpu.circ as structural Verilog: 2 circuits, main circuit Kouachi_proc
module Kouachi_proc (
  input  RESET
);

  wire clock_1_out, PC_plus_plus;
  wire [2:0] counter_1_q;
  wire [11:0] rom_1_data;

  Clock clock_1 (.out(clock_1_out));
  Counter #(.width(3), .max('h7)) counter_1 (
    .count(PC_plus_plus), .Q(counter_1_q), .clk(clock_1_out), .clr(RESET));  // open: load, D, carry
  ROM #(.addrWidth(3), .dataWidth(12)) rom_1 (.addr(counter_1_q), .data(rom_1_data));  // open: sel
endmodule

module IR (
  input  [11:0] Input,
  output [1:0] M_U,
  output [3:0] OPCODE,
  output [1:0] R1,
  output [1:0] R2,
  output [1:0] R3,
  output [3:0] Imm
);


  assign Imm = Input[3:0];
  assign M_U = Input[11:10];
  assign OPCODE = Input[9:6];
  assign R1 = Input[5:4];
  assign R2 = Input[3:2];
  assign R3 = Input[1:0];
endmodule
