// Logisim project UCC.circ as structural Verilog: 1 circuit, main circuit UCC
module UCC (
  input  clk,
  input  Input,
  input  [3:0] OPcode,
  output out_4,
  output out_5,
  output out_6,
  output out_7,
  output out_8,
  output out_9,
  output out_10,
  output out_11,
  output out_12
);

  wire not_1_out, or_1_out;
  wire [4:0] mapeer_1_control, multiplexer_1_out, pc_1_output, rom_1_data;
  wire [6:5] rom_1_data_2;

  Mapeer mapeer_1 (.OPcode(OPcode), .control(mapeer_1_control));
  or or_1 (or_1_out, not_1_out, Input);
  PC pc_1 (.Input(multiplexer_1_out), .Output(pc_1_output), .clk(clk), .write(or_1_out));
  Multiplexer #(.width(5), .enable("false")) multiplexer_1 (
    .in0(mapeer_1_control), .in1(rom_1_data), .out(multiplexer_1_out), .sel(rom_1_data_2[5]));
  not not_1 (not_1_out, rom_1_data_2[6]);
  ROM #(.addrWidth(5), .dataWidth(16)) rom_1 (
    .addr(pc_1_output),
    .data({out_4, out_5, out_6, out_7, out_8, out_9, out_10, out_11, out_12, rom_1_data_2, rom_1_data}));  // open: sel

  // Notes on the sheet:
  //   contents of rom_1 (hex, n*v repeats v):
  //   c018 0 0 0 c018 0 0 0 118
endmodule
